# Fritzing sketch Rubik's_Cube_Schematic (saved by Fritzing 1.0.2b)
circuit board: 8.46667cm x 5.64444cm
breadboards: 1

parts:
  Teensy_4_1 = Teensy 4.1
  Pololu_A1 = Pololu A4988 [package=SO16]
  Pololu_A2 = Pololu A4988 [package=SO16]
  Pololu_A3 = Pololu A4988 [package=SO16]
  Pololu_A4 = Pololu A4988 [package=SO16]
  Pololu_A5 = Pololu A4988 [package=SO16]
  Pololu_A6 = Pololu A4988 [package=SO16]
  M1 = Stepper Motor - Bipolar
  M2 = Stepper Motor - Bipolar
  M3 = Stepper Motor - Bipolar
  M4 = Stepper Motor - Bipolar
  M5 = Stepper Motor - Bipolar
  M6 = Stepper Motor - Bipolar
  M7 = RioRand LM2596
  C2 = Tantalum Capacitor [capacitance=1μF voltage=35V package="200 mil [THT, tantalum]"]  # not connected
  C3 = Tantalum Capacitor [capacitance=1μF voltage=35V package="200 mil [THT, tantalum]"]  # not connected
  C4 = Tantalum Capacitor [capacitance=1μF voltage=35V package="200 mil [THT, tantalum]"]  # not connected
  C5 = Tantalum Capacitor [capacitance=1μF voltage=35V package="200 mil [THT, tantalum]"]  # not connected
  C6 = Tantalum Capacitor [capacitance=1μF voltage=35V package="200 mil [THT, tantalum]"]  # not connected
  C7 = Tantalum Capacitor [capacitance=1μF voltage=35V package="200 mil [THT, tantalum]"]  # not connected
  A1 = Hanmatek HM305

nets:
  GND: Teensy_4_1.GND, Teensy_4_1.GND2, Pololu_A1.GND, Pololu_A2.GND, Pololu_A3.GND, Pololu_A4.GND, Pololu_A5.GND, Pololu_A6.GND, M7.Pin_4
  N1: Teensy_4_1.D0, Pololu_A1.ENABLE, Pololu_A2.ENABLE, Pololu_A3.ENABLE, Pololu_A4.ENABLE, Pololu_A5.ENABLE, Pololu_A6.ENABLE
  N2: Teensy_4_1.D1, Pololu_A2.STEP
  N3: Teensy_4_1.D2, Pololu_A2.DIR
  N4: Teensy_4_1.D3, Pololu_A6.STEP
  N5: Teensy_4_1.D4, Pololu_A6.DIR
  N6: Teensy_4_1.D5, Pololu_A1.STEP
  N7: Teensy_4_1.D6, Pololu_A1.DIR
  N8: Teensy_4_1.D7, Pololu_A4.STEP
  N9: Teensy_4_1.D8, Pololu_A4.DIR
  N10: Teensy_4_1.D9, Pololu_A3.STEP
  N11: Teensy_4_1.D10, Pololu_A3.DIR
  N12: Teensy_4_1.D11, Pololu_A5.STEP
  N13: Teensy_4_1.D12, Pololu_A5.DIR
  VDD: Teensy_4_1.Vin, Pololu_A1.MS1, Pololu_A1.VDD, Pololu_A2.MS1, Pololu_A2.VDD, Pololu_A3.MS1, Pololu_A3.VDD, Pololu_A4.MS1, Pololu_A4.VDD, Pololu_A5.MS1, Pololu_A5.VDD, Pololu_A6.MS1, Pololu_A6.VDD, M7.Pin_3
  N14: Pololu_A1.1B, M4.D
  N15: Pololu_A1.1A, M4.B
  N16: Pololu_A1.2A, M4.C
  N17: Pololu_A1.2B, M4.A
  N18: Pololu_A2.1B, M1.D
  N19: Pololu_A2.1A, M1.B
  N20: Pololu_A2.2A, M1.C
  N21: Pololu_A2.2B, M1.A
  N22: Pololu_A2.VMOT, Pololu_A3.VMOT, Pololu_A4.VMOT, Pololu_A5.VMOT, Pololu_A6.VMOT, M7.Pin_1, A1.Pin_4
  N23: Pololu_A3.1B, M3.D
  N24: Pololu_A3.1A, M3.B
  N25: Pololu_A3.2A, M3.C
  N26: Pololu_A3.2B, M3.A
  N27: Pololu_A4.1B, M5.D
  N28: Pololu_A4.1A, M5.B
  N29: Pololu_A4.2A, M5.C
  N30: Pololu_A4.2B, M5.A
  N31: Pololu_A5.1B, M6.D
  N32: Pololu_A5.1A, M6.B
  N33: Pololu_A5.2A, M6.C
  N34: Pololu_A5.2B, M6.A
  N35: Pololu_A6.1B, M2.D
  N36: Pololu_A6.1A, M2.B
  N37: Pololu_A6.2A, M2.C
  N38: Pololu_A6.2B, M2.A
  N39: M7.Pin_2, A1.Pin_3

custom parts:
  Teensy 4.1: The Teensy is a complete USB-based microcontoller development system, in a very small footprint, capable of implementing many types of projects. All programming is done via the USB port. No special programmer is needed, only a standard micro-USB cable and a PC or Macintosh with a USB port.
  Hanmatek HM305: DC Power Supply 30V5A HM305.

// code stored in the sketch: Rubik_Cube.ino

